# Fritzing sketch WaterSwing circuit (saved by Fritzing 0.9.2b)
breadboards: 1

parts:
  Part1 = Arduino Uno (Rev3)
  R1 = Resistor [tolerance=±5% resistance=10k package=THT]
  RE1 = Rotary Encoder [package=THT]
  S1 = Pushbutton [package="[THT]"]

nets:
  N1: Part1.A0, RE1.EncoderPinC
  N2: Part1.D2, R1.Pin_0, S1.Pin_1, S1.Pin_2
  N3: Part1.5V, RE1.EncoderPinB, S1.Pin_3, S1.Pin_4
  N4: Part1.GND, R1.Pin_1, RE1.EncoderPinA
